// Logisim project Multiplexor.circ as structural Verilog: 1 circuit, main circuit main
module main (
);

  wire and_1_out, and_2_out, and_3_out, and_4_out, not_1_out, not_2_out, or_1_out, undriven, undriven_2,
       undriven_3, undriven_4, undriven_5, undriven_6;

  not not_1 (not_1_out, undriven_5);
  not not_2 (not_2_out, undriven_6);
  and and_1 (and_1_out, undriven_3, not_1_out, not_2_out);
  and and_2 (and_2_out, undriven, not_1_out, undriven_6);
  and and_3 (and_3_out, not_2_out, undriven_4, undriven_5);
  and and_4 (and_4_out, undriven_5, undriven_2, undriven_6);
  or or_1 (or_1_out, and_1_out, and_2_out, and_3_out, and_4_out);

  // Notes on the sheet:
  //   a0
  //   a1
  //   a2
  //   a3
  //   __
  //   c1
  //   __
  //   c2
  //   __
  //   b = c1 c2 a0 + c1 c2 a1 + c1 c2 a2 + c1 c2 a3
  //   __
  //   b
endmodule
